# Fritzing sketch Demo (saved by Fritzing 0.8.5b)
circuit board: 8.46667cm x 5.64444cm
breadboards: 1

parts:
  Voltmeter1 = Voltmeter
  Ohmmeter1 = Ohmmeter
  Amperemeter1 = Amperemeter
  R1 = Resistor [tolerance=±5% resistance=220 package=THT]
  V1 = DC Power [voltage=5]
  LED1 = LED - 5mm [color="Red (633nm)" package="5 mm [THT]"]

nets:
  N1: Voltmeter1.Positive, R1.Pin_0, V1.V+
  N2: Voltmeter1.Com, Ohmmeter1.Positive, Ohmmeter1.Com, Amperemeter1.Positive, Amperemeter1.Com, R1.Pin_1, V1.V-, LED1.cathode, LED1.anode

custom parts:
  Voltmeter: A Standard Multimeter in Current mode
  Ohmmeter: A Standard Multimeter in Current mode
  Amperemeter: A Standard Multimeter in Current mode
